# Fritzing sketch SpotMicro (saved by Fritzing 0.9.3b)

parts:
  Raspberry_Pi_2 = Raspberry Pi 3 [part_number=RPI-3-V1.2]
  Part1 = InvenSense MPU6050
  Part2 = Arduino Nano (Rev3.0)
  hc-sr1 = hc-sr04
  hc-sr2 = hc-sr04
  U2 = LCD-16X2 [package=lcd-16x2]
  Part3 = 16-Channel 12-bit PWM Servo Driver - I2C [part_number=815]
  LCM1602_IIC1 = LCM1602 IIC [part_number="LCM1602 IIC" chip_label="LCM1602 IIC" package="DIP (Dual Inline) [THT]"]
  M1 = RioRand LM2596
  U3 = SWITCH-SPST-2 [package=switch-spst-vertical]
  BATT1 = LiPoly Battery (1300mAh)

nets:
  VCC: Raspberry_Pi_2.3v3, Part1.VCC, Part3.VCC
  N1: Raspberry_Pi_2.GPIO2, Part1.SDA, Part1.XDA, Part3.SDA, LCM1602_IIC1.SDA
  N2: Raspberry_Pi_2.GPIO3, Part1.SCL, Part3.SCL, LCM1602_IIC1.SCL
  GND: Raspberry_Pi_2.GND, Raspberry_Pi_2.GIPO14, Part1.GND, Part2.D0/RX, Part2.RESET, Part2.GND, hc-sr1.GND, hc-sr2.GND, Part3.GND, LCM1602_IIC1.GND, M1.Pin_2, M1.Pin_4, BATT1.negative
  N3: Raspberry_Pi_2.GIPO15, Part2.D1/TX
  5V: Raspberry_Pi_2.5V, Part2.5V, Part2.A7, LCM1602_IIC1.VCC, M1.Pin_3
  VCC_2: Part2.D2, hc-sr1.VCC, hc-sr2.VCC
  N4: Part2.D3, hc-sr2.Trig
  N5: Part2.D4, hc-sr2.Echo
  N6: Part2.D5, hc-sr1.Trig
  N7: Part2.D6, Part2.D7, hc-sr1.Echo
  VSS: U2.VSS, LCM1602_IIC1.VSS
  VDD: U2.VDD, LCM1602_IIC1.VDD
  N8: U2.VO, LCM1602_IIC1.V0
  N9: U2.RS, LCM1602_IIC1.RS
  N10: U2.R_W, LCM1602_IIC1.RW
  N11: U2.E, LCM1602_IIC1.E
  N12: U2.DB0, LCM1602_IIC1.D0
  N13: U2.DB1, LCM1602_IIC1.D1
  N14: U2.DB2, LCM1602_IIC1.D2
  N15: U2.DB3, LCM1602_IIC1.D3
  N16: U2.DB4, LCM1602_IIC1.D4
  N17: U2.DB5, LCM1602_IIC1.D5
  N18: U2.DB6, LCM1602_IIC1.D6
  N19: U2.DB7, LCM1602_IIC1.D7
  N20: U2.A, LCM1602_IIC1.A
  N21: U2.K, LCM1602_IIC1.K
  N22: Part3.PWRIN, M1.Pin_1, U3.O
  N23: LCM1602_IIC1.LED_A, LCM1602_IIC1.LED_B
  N24: U3.P, BATT1.positive

custom parts:
  16-Channel 12-bit PWM Servo Driver - I2C: You want to make a cool robot, maybe a hexapod walker, or maybe just a piece of art with a lot of moving parts. Or maybe you want to drive a lot of LEDs with precise PWM output. Using only two pins, control 16 free-running PWM outputs! You can even chain up 62 breakouts to control up to 992 PWM outputs.
  LCM1602 IIC: I2C-Module to use a 1602 or 2004 LCD on with the wire.h libory Serial LCD Modul
  LiPoly Battery (1300mAh): Lithium Ion Polymer Battery (1300mAh)
